# Fritzing sketch Sabotage-Detection (saved by Fritzing 0.8.6b)
circuit board: 6.88566cm x 5.36311cm
breadboards: 2

parts:
  S2 = Pushbutton [package="[THT]"]
  R6 = Resistor [tolerance=±5% resistance=220 package=THT]
  R7 = Resistor [tolerance=±5% resistance=1.1k package=THT]
  R8 = Resistor [tolerance=±5% resistance=220 package=THT]
  R9 = Resistor [tolerance=±5% resistance=220 package=THT]
  LED6 = LED - 5mm [color="Green (555nm)" package="5 mm [THT]"]
  ADXL335 = Triple Axis Accelerometer Breakout - ADXL335
  LED7 = Super Flux LED blue [color=Red]
  Pot = Rotary Potentiometer (Small) [maximum_resistance=100kΩ package=THT]
  Arduino1 = Arduino Uno (Rev3)
  LED8 = Super Flux LED blue [color=Blue]
  part = Super Flux LED blue [color=Blue]  # not connected

nets:
  N1: S2.Pin_1, S2.Pin_2, Pot.leg1, Arduino1.5V
  N2: S2.Pin_3, S2.Pin_4, R7.Pin_1, Arduino1.D2
  GND: R6.Pin_0, R7.Pin_0, R8.Pin_0, R9.Pin_0, ADXL335.GND, Pot.leg2, Arduino1.GND
  N3: R6.Pin_1, LED6.cathode
  N4: R8.Pin_1, LED7.cathode
  N5: R9.Pin_1, LED8.cathode
  N6: LED6.anode, Arduino1.D11_PWM/MOSI
  N7: ADXL335.ZOUT, Arduino1.A0
  N8: ADXL335.YOUT, Arduino1.A1
  N9: ADXL335.XOUT, Arduino1.A2
  VCC: ADXL335.VCC, Arduino1.3V3
  N10: LED7.anode, Arduino1.D3_PWM
  N11: Pot.wiper, Arduino1.A3
  N12: Arduino1.D7, LED8.anode

notes:
  Get the Arduino Code from here:
  Sabotage Alert
